# Fritzing sketch GardenLite (saved by Fritzing 1.0.6)
breadboards: 1

parts:
  Solar_Panel_2 = Generic Small 6V Solar Panel
  Solar_Panel_1 = Generic Small 6V Solar Panel
  TP4056 = TP4056 [chip_label=TP4056 package="DIP (Dual Inline) [THT]"]
  Li-On = 18650 battery holder [package=battery-18650-kit]
  Switch = Taiway 100-SP-X-T1 SPDT Miniature Toggle Switch [part_number=100-SP-X-T1-0-0-B1-M1 package=THT]
  ESP32-C3 = Esp32-c3 super mini
  IR_LED_strip = smd LED [color="Blue (430nm)" package="0805 [SMD]"]

nets:
  N1: Solar_Panel_2.+, Solar_Panel_1.+, TP4056.pin1
  N2: Solar_Panel_2.-, Solar_Panel_1.-, TP4056.pin2, ESP32-C3.Pin_15, IR_LED_strip.cathode
  N3: TP4056.pin3, ESP32-C3.Pin_16
  N4: TP4056.pin4, Li-On.+
  N5: TP4056.pin5, Switch.COM
  N6: Li-On.-, Switch.L2
  N7: ESP32-C3.Pin_10, IR_LED_strip.anode

custom parts:
  TP4056: A DIP stand-in part for whatever IC you want. With 6 pins on a 300mil dual inline package (DIP) footprint.
  18650 battery holder: 18650 Battery Holder
  Esp32-c3 super mini: ESP32-C3 Development Board ESP32 SuperMini Development Board ESP32 Development Board WiFi Bluetooth.
